// Logisim project FlipFlops.circ as structural Verilog: 5 circuits, main circuit main
module latch_simples (
  input  S,
  input  R,
  output Q,
  output nQ
);

  nor nor_1 (Q, R, nQ);
  nor nor_2 (nQ, Q, S);

  // Notes on the sheet:
  //   Legenda
  //   Q - O output principal.
  //   Descrição
  //   LATCH SIMPLES
  //    não configura um uso adequado do circuito.
  //   S - (SET) Quando verdadeiro, seta o estado para 1.
  //   R - (RESET) Quando verdadeiro, reseta o estado para 0.
  //   nQ - O oposto do output principal. Presente por convenção.
  //   Um latch é um circuito sequencial extremamente simples. 
  //   Tudo o que ele faz é “guardar” um estado booleano (0 ou 1).
  //   É usado como base para os demais flip-flops.
  //   R
  //   S
  //   0
  //   0
  //   0
  //   1
  //   1
  //   0
  //   1
  //   1
  //   Quando o reset recebe um sinal 1, o estado do latch é resetado para 0.
  //   Quando o set recebe um sinal 1, o estado do latch é setado para 1. 
  //   O comportamento do circuito quando S = 1 e R = 1 não está definido e
  //   Tabela de Verdade Reduzida
  //   Q
  //   nQ
  //   0/1
  //   1/0
  //   0
  //   1
  //   1
  //   0
  //   X
  //   X
  //   Não tem versões comerciais. 
  //   R
  //   Qa
  //   S
  //   0
  //   0
  //   0
  //   0
  //   0
  //   1
  //   0
  //   1
  //   0
  //   0
  //   1
  //   1
  //   1
  //   0
  //   0
  //   1
  //   0
  //   1
  //   1
  //   1
  //   0
  //   1
  //   1
  //   1
  //   Tabela de Verdade Extendida
  //   Q
  //   nQ
  //   0
  //   1
  //   1
  //   0
  //   0
  //   1
  //   0
  //   1
  //   1
  //   0
  //   1
  //   0
  //   X
  //   X
  //   X
  //   X
  //   Qa - Estado anterior.
endmodule

module main (
  input  in_1,
  input  in_2,
  input  in_3,
  input  in_4,
  input  in_5,
  input  in_6,
  input  in_7,
  input  in_8
);

  wire flipflop_jk_1_nq, flipflop_jk_1_q, flipflop_rs_1_nq, flipflop_rs_1_q, latch_simples_1_nq,
       latch_simples_1_q;

  LED led_1 (.in(latch_simples_1_q));
  latch_simples latch_simples_1 (.S(in_1), .R(in_2), .Q(latch_simples_1_q), .nQ(latch_simples_1_nq));
  LED led_2 (.in(latch_simples_1_nq));
  LED led_3 (.in(flipflop_rs_1_q));
  flipflop_rs flipflop_rs_1 (.S(in_3), .R(in_4), .CLK(in_5), .Q(flipflop_rs_1_q), .nQ(flipflop_rs_1_nq));
  LED led_4 (.in(flipflop_rs_1_nq));
  LED led_5 (.in(flipflop_jk_1_q));
  flipflop_jk flipflop_jk_1 (.J(in_6), .K(in_7), .CLK(in_8), .Q(flipflop_jk_1_q), .nQ(flipflop_jk_1_nq));
  LED led_6 (.in(flipflop_jk_1_nq));
endmodule

module flipflop_rs (
  input  S,
  input  R,
  input  CLK,
  output Q,
  output nQ
);

  wire and_1_out, and_2_out;

  and and_1 (and_1_out, S, CLK);
  and and_2 (and_2_out, CLK, R);
  nor nor_1 (Q, and_1_out, nQ);
  nor nor_2 (nQ, Q, and_2_out);

  // Notes on the sheet:
  //   Legenda
  //   Descrição
  //   FLIPFLOP RS
  //   Q - O output principal.
  //   S - (SET) Quando verdadeiro, seta o estado para 1.
  //   R - (RESET) Quando verdadeiro, reseta o estado para 0.
  //   nQ - O oposto do output principal. Presente por convenção.
  //   ou seja, imediatamente quando o valor do CLK se torna 1.
  //   CLK - (CLOCK, RELÓGIO em português) Quando verdadeiro, atualiza o estado.
  //   O estado do FF SR se torna 1 quando Set recebe 1 e 0 quando Reset recebe 0. 
  //   Também chamado de Flipflop SR, se trata de um circuito baseado em um Latch simples. 
  //   Lembre-se que S = 1 e R = 1 simultaneamente não configura um uso válido do circuito. 
  //   Diferente de um latch simples, o FF RS apenas muda o seu estado na borda de subida do clock, 
  //   Dessa forma, mesmo se R = 1, o estado Q = 1 se mantem até que o CLK passe a ser 1.
  //   R
  //   S
  //   0
  //   0
  //   0
  //   1
  //   1
  //   0
  //   1
  //   1
  //   Tabela de Verdade Reduzida
  //   Q
  //   nQ
  //   0/1
  //   1/0
  //   0
  //   1
  //   1
  //   0
  //   X
  //   X
  //   R
  //   Qa
  //   S
  //   0
  //   0
  //   0
  //   0
  //   0
  //   1
  //   0
  //   1
  //   0
  //   0
  //   1
  //   1
  //   1
  //   0
  //   0
  //   1
  //   0
  //   1
  //   1
  //   1
  //   0
  //   1
  //   1
  //   1
  //   Qa - Estado anterior.
  //   Tabela de Verdade Extendida
  //   Q
  //   nQ
  //   0
  //   1
  //   1
  //   0
  //   0
  //   1
  //   0
  //   1
  //   1
  //   0
  //   1
  //   0
  //   X
  //   X
  //   X
  //   X
endmodule

module flipflop_jk (
  input  J,
  input  K,
  input  CLK,
  output Q,
  output nQ
);

  wire and_1_out, and_2_out, buffer_1_out, buffer_2_out;

  and and_1 (and_1_out, J, Q, CLK);
  and and_2 (and_2_out, CLK, nQ, K);
  nor nor_1 (Q, and_1_out, buffer_1_out);
  buf buffer_1 (buffer_1_out, nQ);
  buf buffer_2 (buffer_2_out, Q);
  nor nor_2 (nQ, buffer_2_out, and_2_out);

  // Notes on the sheet:
  //   FLIPFLOP JK
endmodule

module nand_flipflop_jk (
  input  J,
  input  K,
  input  CLK,
  output Q,
  output nQ
);

  wire nand_1_out, nand_2_out, not_1_out, not_2_out, not_3_out, not_4_out;

  nand nand_1 (nand_1_out, Q, CLK);
  nand nand_2 (nand_2_out, CLK, nQ);
  not not_1 (not_1_out, nand_1_out);
  or or_1 (Q, not_1_out, not_2_out);
  not not_2 (not_2_out, nQ);
  not not_3 (not_3_out, Q);
  or or_2 (nQ, not_3_out, not_4_out);
  not not_4 (not_4_out, nand_2_out);

  // Notes on the sheet:
  //   FLIPFLOP JK
endmodule
